// Logisim project 19bit_new.circ as structural Verilog: 2 circuits, main circuit main
module main (
);

  wire clock_1_out, cu_1_out_2, cu_1_out_3, cu_1_out_4, cu_1_out_5, cu_1_out_6, cu_1_out_7, cu_1_out_8,
       cu_1_out_9, cu_1_out_10, cu_1_out_11;
  wire [18:0] A_q18, B_q18, C_q18, controlled_buffer_1_out, D_q18, E_q18;

  Clock clock_1 (.out(clock_1_out));
  cu cu_1 (
    .out_7(cu_1_out_7), .out_4(cu_1_out_4), .out_5(cu_1_out_5), .out_6(cu_1_out_6), .out_8(cu_1_out_8),
    .out_9(cu_1_out_9), .out_10(cu_1_out_10), .out_11(cu_1_out_11), .in_1(clock_1_out), .out_3(cu_1_out_3),
    .out_2(cu_1_out_2));
  Shift_Register #(.length(19)) A (
    .shift(1'b0), .clk(clock_1_out), .load(cu_1_out_11), .d0(controlled_buffer_1_out[18]), .q0(A_q18[18]),
    .d1(controlled_buffer_1_out[17]), .q1(A_q18[17]), .d2(controlled_buffer_1_out[16]), .q2(A_q18[16]),
    .d3(controlled_buffer_1_out[15]), .q3(A_q18[15]), .d4(controlled_buffer_1_out[14]), .q4(A_q18[14]),
    .d5(controlled_buffer_1_out[13]), .q5(A_q18[13]), .d6(controlled_buffer_1_out[12]), .q6(A_q18[12]),
    .d7(controlled_buffer_1_out[11]), .q7(A_q18[11]), .d8(controlled_buffer_1_out[10]), .q8(A_q18[10]),
    .d9(controlled_buffer_1_out[9]), .q9(A_q18[9]), .d10(controlled_buffer_1_out[8]), .q10(A_q18[8]),
    .d11(controlled_buffer_1_out[7]), .q11(A_q18[7]), .d12(controlled_buffer_1_out[6]), .q12(A_q18[6]),
    .d13(controlled_buffer_1_out[5]), .q13(A_q18[5]), .d14(controlled_buffer_1_out[4]), .q14(A_q18[4]),
    .d15(controlled_buffer_1_out[3]), .q15(A_q18[3]), .d16(controlled_buffer_1_out[2]), .q16(A_q18[2]),
    .d17(controlled_buffer_1_out[1]), .q17(A_q18[1]), .d18(controlled_buffer_1_out[0]), .q18(A_q18[0]));  // open: in, out, clr
  Shift_Register #(.length(19)) B (
    .shift(1'b0), .clk(clock_1_out), .load(cu_1_out_9), .d0(controlled_buffer_1_out[18]), .q0(B_q18[18]),
    .d1(controlled_buffer_1_out[17]), .q1(B_q18[17]), .d2(controlled_buffer_1_out[16]), .q2(B_q18[16]),
    .d3(controlled_buffer_1_out[15]), .q3(B_q18[15]), .d4(controlled_buffer_1_out[14]), .q4(B_q18[14]),
    .d5(controlled_buffer_1_out[13]), .q5(B_q18[13]), .d6(controlled_buffer_1_out[12]), .q6(B_q18[12]),
    .d7(controlled_buffer_1_out[11]), .q7(B_q18[11]), .d8(controlled_buffer_1_out[10]), .q8(B_q18[10]),
    .d9(controlled_buffer_1_out[9]), .q9(B_q18[9]), .d10(controlled_buffer_1_out[8]), .q10(B_q18[8]),
    .d11(controlled_buffer_1_out[7]), .q11(B_q18[7]), .d12(controlled_buffer_1_out[6]), .q12(B_q18[6]),
    .d13(controlled_buffer_1_out[5]), .q13(B_q18[5]), .d14(controlled_buffer_1_out[4]), .q14(B_q18[4]),
    .d15(controlled_buffer_1_out[3]), .q15(B_q18[3]), .d16(controlled_buffer_1_out[2]), .q16(B_q18[2]),
    .d17(controlled_buffer_1_out[1]), .q17(B_q18[1]), .d18(controlled_buffer_1_out[0]), .q18(B_q18[0]));  // open: in, out, clr
  Shift_Register #(.length(19)) C (
    .shift(1'b0), .clk(clock_1_out), .load(cu_1_out_7), .d0(controlled_buffer_1_out[18]), .q0(C_q18[18]),
    .d1(controlled_buffer_1_out[17]), .q1(C_q18[17]), .d2(controlled_buffer_1_out[16]), .q2(C_q18[16]),
    .d3(controlled_buffer_1_out[15]), .q3(C_q18[15]), .d4(controlled_buffer_1_out[14]), .q4(C_q18[14]),
    .d5(controlled_buffer_1_out[13]), .q5(C_q18[13]), .d6(controlled_buffer_1_out[12]), .q6(C_q18[12]),
    .d7(controlled_buffer_1_out[11]), .q7(C_q18[11]), .d8(controlled_buffer_1_out[10]), .q8(C_q18[10]),
    .d9(controlled_buffer_1_out[9]), .q9(C_q18[9]), .d10(controlled_buffer_1_out[8]), .q10(C_q18[8]),
    .d11(controlled_buffer_1_out[7]), .q11(C_q18[7]), .d12(controlled_buffer_1_out[6]), .q12(C_q18[6]),
    .d13(controlled_buffer_1_out[5]), .q13(C_q18[5]), .d14(controlled_buffer_1_out[4]), .q14(C_q18[4]),
    .d15(controlled_buffer_1_out[3]), .q15(C_q18[3]), .d16(controlled_buffer_1_out[2]), .q16(C_q18[2]),
    .d17(controlled_buffer_1_out[1]), .q17(C_q18[1]), .d18(controlled_buffer_1_out[0]), .q18(C_q18[0]));  // open: in, out, clr
  Shift_Register #(.length(19)) D (
    .shift(1'b0), .clk(clock_1_out), .load(cu_1_out_5), .d0(controlled_buffer_1_out[18]), .q0(D_q18[18]),
    .d1(controlled_buffer_1_out[17]), .q1(D_q18[17]), .d2(controlled_buffer_1_out[16]), .q2(D_q18[16]),
    .d3(controlled_buffer_1_out[15]), .q3(D_q18[15]), .d4(controlled_buffer_1_out[14]), .q4(D_q18[14]),
    .d5(controlled_buffer_1_out[13]), .q5(D_q18[13]), .d6(controlled_buffer_1_out[12]), .q6(D_q18[12]),
    .d7(controlled_buffer_1_out[11]), .q7(D_q18[11]), .d8(controlled_buffer_1_out[10]), .q8(D_q18[10]),
    .d9(controlled_buffer_1_out[9]), .q9(D_q18[9]), .d10(controlled_buffer_1_out[8]), .q10(D_q18[8]),
    .d11(controlled_buffer_1_out[7]), .q11(D_q18[7]), .d12(controlled_buffer_1_out[6]), .q12(D_q18[6]),
    .d13(controlled_buffer_1_out[5]), .q13(D_q18[5]), .d14(controlled_buffer_1_out[4]), .q14(D_q18[4]),
    .d15(controlled_buffer_1_out[3]), .q15(D_q18[3]), .d16(controlled_buffer_1_out[2]), .q16(D_q18[2]),
    .d17(controlled_buffer_1_out[1]), .q17(D_q18[1]), .d18(controlled_buffer_1_out[0]), .q18(D_q18[0]));  // open: in, out, clr
  Shift_Register #(.length(19)) E (
    .shift(1'b0), .clk(clock_1_out), .load(cu_1_out_3), .d0(controlled_buffer_1_out[18]), .q0(E_q18[18]),
    .d1(controlled_buffer_1_out[17]), .q1(E_q18[17]), .d2(controlled_buffer_1_out[16]), .q2(E_q18[16]),
    .d3(controlled_buffer_1_out[15]), .q3(E_q18[15]), .d4(controlled_buffer_1_out[14]), .q4(E_q18[14]),
    .d5(controlled_buffer_1_out[13]), .q5(E_q18[13]), .d6(controlled_buffer_1_out[12]), .q6(E_q18[12]),
    .d7(controlled_buffer_1_out[11]), .q7(E_q18[11]), .d8(controlled_buffer_1_out[10]), .q8(E_q18[10]),
    .d9(controlled_buffer_1_out[9]), .q9(E_q18[9]), .d10(controlled_buffer_1_out[8]), .q10(E_q18[8]),
    .d11(controlled_buffer_1_out[7]), .q11(E_q18[7]), .d12(controlled_buffer_1_out[6]), .q12(E_q18[6]),
    .d13(controlled_buffer_1_out[5]), .q13(E_q18[5]), .d14(controlled_buffer_1_out[4]), .q14(E_q18[4]),
    .d15(controlled_buffer_1_out[3]), .q15(E_q18[3]), .d16(controlled_buffer_1_out[2]), .q16(E_q18[2]),
    .d17(controlled_buffer_1_out[1]), .q17(E_q18[1]), .d18(controlled_buffer_1_out[0]), .q18(E_q18[0]));  // open: in, out, clr
  assign controlled_buffer_1_out = cu_1_out_10 ? A_q18 : 19'bz;  // Controlled_Buffer controlled_buffer_1
  assign controlled_buffer_1_out = cu_1_out_8 ? B_q18 : 19'bz;  // Controlled_Buffer controlled_buffer_2
  assign controlled_buffer_1_out = cu_1_out_6 ? C_q18 : 19'bz;  // Controlled_Buffer controlled_buffer_3
  assign controlled_buffer_1_out = cu_1_out_4 ? D_q18 : 19'bz;  // Controlled_Buffer controlled_buffer_4
  assign controlled_buffer_1_out = cu_1_out_2 ? E_q18 : 19'bz;  // Controlled_Buffer controlled_buffer_5

  // Notes on the sheet:
  //                                        A -> E -> B -> D -> E
  //   Sequence:
endmodule

module cu (
  input  in_1,
  output out_2,
  output out_3,
  output out_4,
  output out_5,
  output out_6,
  output out_7,
  output out_8,
  output out_9,
  output out_10,
  output out_11
);

  wire [1:0] counter_1_q;
  wire [11:10] rom_1_data;

  Counter #(.width(2), .max('h3)) counter_1 (.Q(counter_1_q), .clk(in_1));  // open: load, D, count, carry, clr
  ROM #(.addrWidth(2), .dataWidth(12)) rom_1 (
    .addr(counter_1_q),
    .data({rom_1_data, out_11, out_10, out_9, out_8, out_7, out_6, out_5, out_4, out_3, out_2}));  // open: sel

  // Notes on the sheet:
  //   contents of rom_1 (hex, n*v repeats v):
  //   102 81 48 6
endmodule
