// Logisim project amarhatesobcontrol.circ as structural Verilog: 2 circuits, main circuit main
module main (
);

  wire clock_1_out, cu_1_out_2, cu_1_out_3, cu_1_out_4, cu_1_out_5, cu_1_out_6, cu_1_out_7, cu_1_out_8,
       cu_1_out_9, cu_1_out_10, cu_1_out_11;
  wire [27:0] A_q27, B_q27, C_q27, controlled_buffer_1_out, D_q27, E_q27;

  Clock clock_1 (.out(clock_1_out));
  cu cu_1 (
    .out_7(cu_1_out_7), .out_4(cu_1_out_4), .out_5(cu_1_out_5), .out_6(cu_1_out_6), .out_8(cu_1_out_8),
    .out_9(cu_1_out_9), .out_10(cu_1_out_10), .out_11(cu_1_out_11), .in_1(clock_1_out), .out_3(cu_1_out_3),
    .out_2(cu_1_out_2));
  Shift_Register #(.length(28)) A (
    .shift(cu_1_out_11), .clk(clock_1_out), .load(cu_1_out_11), .d0(controlled_buffer_1_out[27]),
    .q0(A_q27[27]), .d1(controlled_buffer_1_out[26]), .q1(A_q27[26]), .d2(controlled_buffer_1_out[25]),
    .q2(A_q27[25]), .d3(controlled_buffer_1_out[24]), .q3(A_q27[24]), .d4(controlled_buffer_1_out[23]),
    .q4(A_q27[23]), .d5(controlled_buffer_1_out[22]), .q5(A_q27[22]), .d6(controlled_buffer_1_out[21]),
    .q6(A_q27[21]), .d7(controlled_buffer_1_out[20]), .q7(A_q27[20]), .d8(controlled_buffer_1_out[19]),
    .q8(A_q27[19]), .d9(controlled_buffer_1_out[18]), .q9(A_q27[18]), .d10(controlled_buffer_1_out[17]),
    .q10(A_q27[17]), .d11(controlled_buffer_1_out[16]), .q11(A_q27[16]), .d12(controlled_buffer_1_out[15]),
    .q12(A_q27[15]), .d13(controlled_buffer_1_out[14]), .q13(A_q27[14]), .d14(controlled_buffer_1_out[13]),
    .q14(A_q27[13]), .d15(controlled_buffer_1_out[12]), .q15(A_q27[12]), .d16(controlled_buffer_1_out[11]),
    .q16(A_q27[11]), .d17(controlled_buffer_1_out[10]), .q17(A_q27[10]), .d18(controlled_buffer_1_out[9]),
    .q18(A_q27[9]), .d19(controlled_buffer_1_out[8]), .q19(A_q27[8]), .d20(controlled_buffer_1_out[7]),
    .q20(A_q27[7]), .d21(controlled_buffer_1_out[6]), .q21(A_q27[6]), .d22(controlled_buffer_1_out[5]),
    .q22(A_q27[5]), .d23(controlled_buffer_1_out[4]), .q23(A_q27[4]), .d24(controlled_buffer_1_out[3]),
    .q24(A_q27[3]), .d25(controlled_buffer_1_out[2]), .q25(A_q27[2]), .d26(controlled_buffer_1_out[1]),
    .q26(A_q27[1]), .d27(controlled_buffer_1_out[0]), .q27(A_q27[0]));  // open: in, out, clr
  Shift_Register #(.length(28)) B (
    .shift(cu_1_out_9), .clk(clock_1_out), .load(cu_1_out_9), .d0(controlled_buffer_1_out[27]),
    .q0(B_q27[27]), .d1(controlled_buffer_1_out[26]), .q1(B_q27[26]), .d2(controlled_buffer_1_out[25]),
    .q2(B_q27[25]), .d3(controlled_buffer_1_out[24]), .q3(B_q27[24]), .d4(controlled_buffer_1_out[23]),
    .q4(B_q27[23]), .d5(controlled_buffer_1_out[22]), .q5(B_q27[22]), .d6(controlled_buffer_1_out[21]),
    .q6(B_q27[21]), .d7(controlled_buffer_1_out[20]), .q7(B_q27[20]), .d8(controlled_buffer_1_out[19]),
    .q8(B_q27[19]), .d9(controlled_buffer_1_out[18]), .q9(B_q27[18]), .d10(controlled_buffer_1_out[17]),
    .q10(B_q27[17]), .d11(controlled_buffer_1_out[16]), .q11(B_q27[16]), .d12(controlled_buffer_1_out[15]),
    .q12(B_q27[15]), .d13(controlled_buffer_1_out[14]), .q13(B_q27[14]), .d14(controlled_buffer_1_out[13]),
    .q14(B_q27[13]), .d15(controlled_buffer_1_out[12]), .q15(B_q27[12]), .d16(controlled_buffer_1_out[11]),
    .q16(B_q27[11]), .d17(controlled_buffer_1_out[10]), .q17(B_q27[10]), .d18(controlled_buffer_1_out[9]),
    .q18(B_q27[9]), .d19(controlled_buffer_1_out[8]), .q19(B_q27[8]), .d20(controlled_buffer_1_out[7]),
    .q20(B_q27[7]), .d21(controlled_buffer_1_out[6]), .q21(B_q27[6]), .d22(controlled_buffer_1_out[5]),
    .q22(B_q27[5]), .d23(controlled_buffer_1_out[4]), .q23(B_q27[4]), .d24(controlled_buffer_1_out[3]),
    .q24(B_q27[3]), .d25(controlled_buffer_1_out[2]), .q25(B_q27[2]), .d26(controlled_buffer_1_out[1]),
    .q26(B_q27[1]), .d27(controlled_buffer_1_out[0]), .q27(B_q27[0]));  // open: in, out, clr
  Shift_Register #(.length(28)) C (
    .shift(cu_1_out_7), .clk(clock_1_out), .load(cu_1_out_7), .d0(controlled_buffer_1_out[27]),
    .q0(C_q27[27]), .d1(controlled_buffer_1_out[26]), .q1(C_q27[26]), .d2(controlled_buffer_1_out[25]),
    .q2(C_q27[25]), .d3(controlled_buffer_1_out[24]), .q3(C_q27[24]), .d4(controlled_buffer_1_out[23]),
    .q4(C_q27[23]), .d5(controlled_buffer_1_out[22]), .q5(C_q27[22]), .d6(controlled_buffer_1_out[21]),
    .q6(C_q27[21]), .d7(controlled_buffer_1_out[20]), .q7(C_q27[20]), .d8(controlled_buffer_1_out[19]),
    .q8(C_q27[19]), .d9(controlled_buffer_1_out[18]), .q9(C_q27[18]), .d10(controlled_buffer_1_out[17]),
    .q10(C_q27[17]), .d11(controlled_buffer_1_out[16]), .q11(C_q27[16]), .d12(controlled_buffer_1_out[15]),
    .q12(C_q27[15]), .d13(controlled_buffer_1_out[14]), .q13(C_q27[14]), .d14(controlled_buffer_1_out[13]),
    .q14(C_q27[13]), .d15(controlled_buffer_1_out[12]), .q15(C_q27[12]), .d16(controlled_buffer_1_out[11]),
    .q16(C_q27[11]), .d17(controlled_buffer_1_out[10]), .q17(C_q27[10]), .d18(controlled_buffer_1_out[9]),
    .q18(C_q27[9]), .d19(controlled_buffer_1_out[8]), .q19(C_q27[8]), .d20(controlled_buffer_1_out[7]),
    .q20(C_q27[7]), .d21(controlled_buffer_1_out[6]), .q21(C_q27[6]), .d22(controlled_buffer_1_out[5]),
    .q22(C_q27[5]), .d23(controlled_buffer_1_out[4]), .q23(C_q27[4]), .d24(controlled_buffer_1_out[3]),
    .q24(C_q27[3]), .d25(controlled_buffer_1_out[2]), .q25(C_q27[2]), .d26(controlled_buffer_1_out[1]),
    .q26(C_q27[1]), .d27(controlled_buffer_1_out[0]), .q27(C_q27[0]));  // open: in, out, clr
  Shift_Register #(.length(28)) D (
    .shift(cu_1_out_5), .clk(clock_1_out), .load(cu_1_out_5), .d0(controlled_buffer_1_out[27]),
    .q0(D_q27[27]), .d1(controlled_buffer_1_out[26]), .q1(D_q27[26]), .d2(controlled_buffer_1_out[25]),
    .q2(D_q27[25]), .d3(controlled_buffer_1_out[24]), .q3(D_q27[24]), .d4(controlled_buffer_1_out[23]),
    .q4(D_q27[23]), .d5(controlled_buffer_1_out[22]), .q5(D_q27[22]), .d6(controlled_buffer_1_out[21]),
    .q6(D_q27[21]), .d7(controlled_buffer_1_out[20]), .q7(D_q27[20]), .d8(controlled_buffer_1_out[19]),
    .q8(D_q27[19]), .d9(controlled_buffer_1_out[18]), .q9(D_q27[18]), .d10(controlled_buffer_1_out[17]),
    .q10(D_q27[17]), .d11(controlled_buffer_1_out[16]), .q11(D_q27[16]), .d12(controlled_buffer_1_out[15]),
    .q12(D_q27[15]), .d13(controlled_buffer_1_out[14]), .q13(D_q27[14]), .d14(controlled_buffer_1_out[13]),
    .q14(D_q27[13]), .d15(controlled_buffer_1_out[12]), .q15(D_q27[12]), .d16(controlled_buffer_1_out[11]),
    .q16(D_q27[11]), .d17(controlled_buffer_1_out[10]), .q17(D_q27[10]), .d18(controlled_buffer_1_out[9]),
    .q18(D_q27[9]), .d19(controlled_buffer_1_out[8]), .q19(D_q27[8]), .d20(controlled_buffer_1_out[7]),
    .q20(D_q27[7]), .d21(controlled_buffer_1_out[6]), .q21(D_q27[6]), .d22(controlled_buffer_1_out[5]),
    .q22(D_q27[5]), .d23(controlled_buffer_1_out[4]), .q23(D_q27[4]), .d24(controlled_buffer_1_out[3]),
    .q24(D_q27[3]), .d25(controlled_buffer_1_out[2]), .q25(D_q27[2]), .d26(controlled_buffer_1_out[1]),
    .q26(D_q27[1]), .d27(controlled_buffer_1_out[0]), .q27(D_q27[0]));  // open: in, out, clr
  Shift_Register #(.length(28)) E (
    .shift(cu_1_out_3), .clk(clock_1_out), .load(cu_1_out_3), .d0(controlled_buffer_1_out[27]),
    .q0(E_q27[27]), .d1(controlled_buffer_1_out[26]), .q1(E_q27[26]), .d2(controlled_buffer_1_out[25]),
    .q2(E_q27[25]), .d3(controlled_buffer_1_out[24]), .q3(E_q27[24]), .d4(controlled_buffer_1_out[23]),
    .q4(E_q27[23]), .d5(controlled_buffer_1_out[22]), .q5(E_q27[22]), .d6(controlled_buffer_1_out[21]),
    .q6(E_q27[21]), .d7(controlled_buffer_1_out[20]), .q7(E_q27[20]), .d8(controlled_buffer_1_out[19]),
    .q8(E_q27[19]), .d9(controlled_buffer_1_out[18]), .q9(E_q27[18]), .d10(controlled_buffer_1_out[17]),
    .q10(E_q27[17]), .d11(controlled_buffer_1_out[16]), .q11(E_q27[16]), .d12(controlled_buffer_1_out[15]),
    .q12(E_q27[15]), .d13(controlled_buffer_1_out[14]), .q13(E_q27[14]), .d14(controlled_buffer_1_out[13]),
    .q14(E_q27[13]), .d15(controlled_buffer_1_out[12]), .q15(E_q27[12]), .d16(controlled_buffer_1_out[11]),
    .q16(E_q27[11]), .d17(controlled_buffer_1_out[10]), .q17(E_q27[10]), .d18(controlled_buffer_1_out[9]),
    .q18(E_q27[9]), .d19(controlled_buffer_1_out[8]), .q19(E_q27[8]), .d20(controlled_buffer_1_out[7]),
    .q20(E_q27[7]), .d21(controlled_buffer_1_out[6]), .q21(E_q27[6]), .d22(controlled_buffer_1_out[5]),
    .q22(E_q27[5]), .d23(controlled_buffer_1_out[4]), .q23(E_q27[4]), .d24(controlled_buffer_1_out[3]),
    .q24(E_q27[3]), .d25(controlled_buffer_1_out[2]), .q25(E_q27[2]), .d26(controlled_buffer_1_out[1]),
    .q26(E_q27[1]), .d27(controlled_buffer_1_out[0]), .q27(E_q27[0]));  // open: in, out, clr
  assign controlled_buffer_1_out = cu_1_out_10 ? A_q27 : 28'bz;  // Controlled_Buffer controlled_buffer_1
  assign controlled_buffer_1_out = cu_1_out_8 ? B_q27 : 28'bz;  // Controlled_Buffer controlled_buffer_2
  assign controlled_buffer_1_out = cu_1_out_6 ? C_q27 : 28'bz;  // Controlled_Buffer controlled_buffer_3
  assign controlled_buffer_1_out = cu_1_out_4 ? D_q27 : 28'bz;  // Controlled_Buffer controlled_buffer_4
  assign controlled_buffer_1_out = cu_1_out_2 ? E_q27 : 28'bz;  // Controlled_Buffer controlled_buffer_5
endmodule

module cu (
  input  in_1,
  output out_2,
  output out_3,
  output out_4,
  output out_5,
  output out_6,
  output out_7,
  output out_8,
  output out_9,
  output out_10,
  output out_11
);

  wire [1:0] counter_1_q;
  wire [11:10] rom_1_data;

  Counter #(.width(2), .max('h3)) counter_1 (.Q(counter_1_q), .clk(in_1));  // open: load, D, count, carry, clr
  ROM #(.addrWidth(2), .dataWidth(12)) rom_1 (
    .addr(counter_1_q),
    .data({rom_1_data, out_11, out_10, out_9, out_8, out_7, out_6, out_5, out_4, out_3, out_2}));  // open: sel

  // Notes on the sheet:
  //   contents of rom_1 (hex, n*v repeats v):
  //   120 90 60 90
endmodule
