// Logisim project lab3.circ as structural Verilog: 1 circuit, main circuit main
module main (
  input  [17:0] in_1,
  input  in_2
);

  wire clock_1_out, undriven;
  wire [2:0] counter_1_q;
  wire [7:0] rom_1_data;
  wire [17:0] A_q, B_q, C_q, D_q, E_q, multiplexer_1_out;

  Multiplexer #(.select(3), .width(18)) multiplexer_1 (
    .in0(in_1), .in1(A_q), .in2(B_q), .in3(C_q), .in4(D_q), .in5(E_q), .in6({18{1'b0}}), .in7({18{1'b0}}),
    .out(multiplexer_1_out), .sel(rom_1_data[7:5]));  // open: en
  Clock clock_1 (.out(clock_1_out));
  Counter #(.width(3), .max('h7)) counter_1 (
    .Q(counter_1_q), .clk(clock_1_out), .clr(undriven));  // open: load, D, count, carry
  Register #(.width(18)) A (.D(multiplexer_1_out), .en(rom_1_data[4]), .Q(A_q), .clk(clock_1_out));  // open: clr
  Register #(.width(18)) B (.D(multiplexer_1_out), .en(rom_1_data[3]), .Q(B_q), .clk(clock_1_out));  // open: clr
  ROM #(.addrWidth(3)) rom_1 (.addr(counter_1_q), .data(rom_1_data));  // open: sel
  Register #(.width(18)) C (.D(multiplexer_1_out), .en(rom_1_data[2]), .Q(C_q), .clk(clock_1_out));  // open: clr
  Register #(.width(18)) D (.D(multiplexer_1_out), .en(rom_1_data[1]), .Q(D_q), .clk(clock_1_out));  // open: clr
  Register #(.width(18)) E (.D(multiplexer_1_out), .en(rom_1_data[0]), .Q(E_q), .clk(clock_1_out));  // open: clr

  // Notes on the sheet:
  //   contents of rom_1 (hex, n*v repeats v):
  //   2 88 42 90 24
endmodule
